# Fritzing sketch gameclock - breadboard (saved by Fritzing 0.9.3b)
breadboards: 1
perfboards: 1

parts:
  LCD1 = LCD screen
  J1 = Piezo Speaker
  R1 = Rotary Potentiometer (Small) [maximum_resistance=100kΩ package=THT]
  R5 = Resistor [tolerance=±5% resistance=10k package=THT]
  C6 = Ceramic Capacitor [capacitance=100nF package="100 mil [THT, multilayer]"]
  S4 = Toggle Switch [package=THT]
  R6 = Resistor [tolerance=±5% resistance=10k package=THT]
  R7 = Resistor [tolerance=±5% resistance=10k package=THT]
  Composant1 = Arduino Nano (Rev3.0)
  ENCODER1 = Rotary_Encoder_with_Knob
  R8 = Resistor [tolerance=±5% resistance=10k package=THT]
  R9 = Resistor [tolerance=±5% resistance=10k package=THT]
  R10 = Resistor [tolerance=±5% resistance=10k package=THT]
  R11 = Resistor [tolerance=±5% resistance=10k package=THT]
  C4 = Ceramic Capacitor [capacitance=100nF package="100 mil [THT, multilayer]"]
  C6_2 = Ceramic Capacitor [capacitance=100nF package="100 mil [THT, multilayer]"]

nets (from the breadboard view):
  N1: LCD1.VSS, LCD1.R/W, J1.pin1, R1.leg1, C6.0, R6.Pin_1, R7.Pin_1, ENCODER1.connector2, ENCODER1.connector5, R8.Pin_0, C4.1, C6_2.1
  N2: LCD1.VDD, R1.leg2, S4.COM, R10.Pin_0, R11.Pin_0
  N3: LCD1.V0, R1.wiper
  N4: LCD1.RS, Composant1.D7
  N5: LCD1.E, Composant1.D6
  N6: LCD1.DB4, Composant1.D5
  N7: LCD1.DB5, Composant1.D4
  N8: LCD1.DB6, Composant1.D3
  N9: LCD1.DB7, Composant1.D2
  N10: J1.pin2, Composant1.D12/MISO
  N11: R5.Pin_0, ENCODER1.connector3, R11.Pin_1
  N12: R5.Pin_1, Composant1.D9, C6_2.0
  N13: C6.1, Composant1.D8, R9.Pin_0
  N14: S4.L1, R6.Pin_0, Composant1.A4
  N15: S4.L2, R7.Pin_0, Composant1.A5
  N16: Composant1.D10, ENCODER1.connector4, R8.Pin_1, C4.0
  N17: ENCODER1.connector1, R9.Pin_1, R10.Pin_1
