# Fritzing sketch gameclock - circuit (saved by Fritzing 0.9.3b)
circuit board: 6.76806cm x 4.7412cm
perfboards: 2
breadboards: 1

parts:
  Rotary_r4 = Resistor [tolerance=±5% resistance=10k package=THT]
  Rotary_C1 = Ceramic Capacitor [capacitance=100nF package="100 mil [THT, multilayer]"]
  Rotary_r2 = Resistor [tolerance=±5% resistance=10k package=THT]
  Rotary_r1 = Resistor [tolerance=±5% resistance=10k package=THT]
  ARDUINO_DIGI = female pin header, 15 pins [form="♀ (female)"]
  ARDUINO_power = female pin header, 15 pins [form="♀ (female)"]
  RetroLight_switch = female pin header, 2 pins [form="♀ (female)"]
  Contrast_Potar = female pin header, 3 pins [form="♀ (female)"]
  LCD_POWER = female pin header, 6 pins [form="♀ (female)"]
  Power_switch = female pin header, 2 pins [form="♀ (female)"]
  Rotary_encoder = female pin header, 5 pins [form="♀ (female)"]
  Player_Toggle_Button = female pin header, 3 pins [form="♀ (female)"]
  Power_Supply = Battery block 9V
  Speaker = Piezo Speaker
  Rotary_r5 = Resistor [tolerance=±5% resistance=10k package=THT]
  player_r1 = Resistor [tolerance=±5% resistance=10k package=THT]
  player_r2 = Resistor [tolerance=±5% resistance=10k package=THT]
  R12 = Resistor [tolerance=±5% resistance=1k package=THT]
  Rotary_C2 = Ceramic Capacitor [capacitance=100nF package="100 mil [THT, multilayer]"]
  LCD_data = female pin header, 6 pins [form="♀ (female)"]
  Rotary_r3 = Resistor [tolerance=±5% resistance=10k package=THT]

nets:
  N1: Rotary_r4.Pin_0, ARDUINO_DIGI.pin4, Rotary_C2.0
  N2: Rotary_r4.Pin_1, Rotary_r2.Pin_1, Rotary_encoder.pin3
  N3: Rotary_C1.0, ARDUINO_DIGI.pin12, ARDUINO_power.pin14, RetroLight_switch.pin1, Contrast_Potar.pin3, LCD_POWER.pin1, Rotary_encoder.pin2, Rotary_encoder.pin4, Power_Supply.-, Speaker.pin1, player_r1.Pin_0, player_r2.Pin_0, Rotary_C2.1
  N4: Rotary_C1.1, ARDUINO_DIGI.pin5, Rotary_r3.Pin_1
  N5: Rotary_r2.Pin_0, Rotary_r1.Pin_0, ARDUINO_power.pin12, Contrast_Potar.pin1, LCD_POWER.pin2, Player_Toggle_Button.pin2, LCD_data.pin5
  N6: Rotary_r1.Pin_1, Rotary_encoder.pin1, Rotary_r3.Pin_0
  N7: ARDUINO_DIGI.pin3, Rotary_r5.Pin_1
  N8: ARDUINO_DIGI.pin6, LCD_POWER.pin4
  N9: ARDUINO_DIGI.pin7, LCD_POWER.pin6
  N10: ARDUINO_DIGI.pin8, LCD_data.pin1
  N11: ARDUINO_DIGI.pin9, LCD_data.pin2
  N12: ARDUINO_DIGI.pin10, LCD_data.pin3
  N13: ARDUINO_DIGI.pin11, LCD_data.pin4
  N14: ARDUINO_power.pin8, Player_Toggle_Button.pin1, player_r2.Pin_1
  N15: ARDUINO_power.pin9, Player_Toggle_Button.pin3, player_r1.Pin_1
  N16: ARDUINO_power.pin15, Power_switch.pin2
  N17: RetroLight_switch.pin2, R12.Pin_0
  N18: Contrast_Potar.pin2, LCD_POWER.pin3
  N19: Power_switch.pin1, Power_Supply.+
  N20: Rotary_encoder.pin5, Rotary_r5.Pin_0
  N21: R12.Pin_1, LCD_data.pin6
